// Logisim project TallerLogica-Combinatorios.circ as structural Verilog: 9 circuits, main circuit verificador
module sumador_simple (
  input  A,
  input  B,
  output S,
  output Cout
);

  wire and_1_out, and_2_out, not_1_out, not_2_out;

  not not_1 (not_1_out, A);
  not not_2 (not_2_out, B);
  and and_1 (and_1_out, not_1_out, B);
  and and_2 (and_2_out, A, not_2_out);
  and and_3 (Cout, A, B);
  or or_1 (S, and_1_out, and_2_out);
endmodule

module sumador_completo (
  input  A,
  input  B,
  input  Cin,
  output S,
  output Cout
);

  wire sumador_simple_1_cout, sumador_simple_1_s, sumador_simple_2_cout;

  sumador_simple sumador_simple_1 (.A(A), .B(B), .S(sumador_simple_1_s), .Cout(sumador_simple_1_cout));
  sumador_simple sumador_simple_2 (.A(sumador_simple_1_s), .B(Cin), .S(S), .Cout(sumador_simple_2_cout));
  or or_1 (Cout, sumador_simple_2_cout, sumador_simple_1_cout);
endmodule

module sumador_4 (
  input  Cin,
  input  [3:0] A,
  input  [3:0] B,
  output [3:0] S,
  output Cout
);

  wire sumador_completo_1_cout, sumador_completo_2_cout, sumador_completo_3_cout;

  sumador_completo sumador_completo_1 (.A(A[0]), .B(B[0]), .Cin(Cin), .S(S[0]), .Cout(sumador_completo_1_cout));
  sumador_completo sumador_completo_2 (
    .A(A[1]), .B(B[1]), .Cin(sumador_completo_1_cout), .S(S[1]), .Cout(sumador_completo_2_cout));
  sumador_completo sumador_completo_3 (
    .A(A[2]), .B(B[2]), .Cin(sumador_completo_2_cout), .S(S[2]), .Cout(sumador_completo_3_cout));
  sumador_completo sumador_completo_4 (.A(A[3]), .B(B[3]), .Cin(sumador_completo_3_cout), .S(S[3]), .Cout(Cout));
  Hex_Digit_Display hex_digit_display_1 (.value(S));  // open: dp
endmodule

module comparador_cero (
  input  [3:0] A,
  output Z
);

  wire nor_1_out, nor_2_out;

  nor nor_1 (nor_1_out, A[0], A[1]);
  nor nor_2 (nor_2_out, A[2], A[3]);
  and and_1 (Z, nor_1_out, nor_2_out);
endmodule

module sumador_flags (
  input  Cin,
  input  [3:0] A,
  input  [3:0] B,
  output [3:0] S,
  output Z,
  output V,
  output N,
  output C
);

  wire and_1_out, and_2_out, and_3_out, and_4_out, not_1_out, not_2_out, not_3_out;

  not not_1 (not_1_out, A[3]);
  not not_2 (not_2_out, B[3]);
  and and_1 (and_1_out, A[3], B[3]);
  and and_2 (and_2_out, not_1_out, not_2_out);
  sumador_4 sumador_4_1 (.Cin(Cin), .A(A), .B(B), .S({N, S[2:0]}), .Cout(C));
  not not_3 (not_3_out, N);
  comparador_cero comparador_cero_1 (.A({N, S[2:0]}), .Z(Z));
  and and_3 (and_3_out, not_3_out, and_1_out);
  and and_4 (and_4_out, N, and_2_out);
  Hex_Digit_Display hex_digit_display_1 (.value({N, S[2:0]}));  // open: dp
  or or_1 (V, and_3_out, and_4_out);

  assign S[3] = N;

  // Notes on the sheet:
  //   sensor_msb_igual
  //   detector_negativo
  //   detector_overflow
  //   msbs_distintos
endmodule

module incrementador_4 (
  input  [3:0] A,
  output [3:0] S
);

  sumador_4 sumador_4_1 (.A(A), .B(4'b0001), .S(S));  // open: Cin, Cout
  Hex_Digit_Display hex_digit_display_1 (.value(S));  // open: dp
endmodule

module inversor_4 (
  input  [3:0] A,
  input  INV,
  output [3:0] S
);

  wire [3:0] incrementador_4_1_s, not_1_out;

  not not_1 (not_1_out[0], A[0]);
  not not_2 (not_1_out[1], A[1]);
  not not_3 (not_1_out[2], A[2]);
  not not_4 (not_1_out[3], A[3]);
  Hex_Digit_Display hex_digit_display_1 (.value(S));  // open: dp
  Multiplexer #(.width(4)) multiplexer_1 (.in0(A), .in1(incrementador_4_1_s), .out(S), .sel(INV));
  incrementador_4 incrementador_4_1 (.A(not_1_out), .S(incrementador_4_1_s));
endmodule

module ALU (
  input  [3:0] A,
  input  [3:0] B,
  input  [1:0] OP,
  input  modo_sin_signo,
  output N,
  output Z,
  output V,
  output C,
  output [3:0] S
);

  wire and_5_out, and_6_out, and_7_out, and_8_out, and_9_out, and_10_out, and_11_out, comparador_cero_1_z,
       comparador_cero_2_z, multiplexer_1_out, multiplexer_3_out, multiplexer_5_out, multiplexer_7_out,
       not_1_out, not_2_out, not_3_out, not_4_out, not_5_out, not_6_out, op11_out, sumador_flags_1_c,
       sumador_flags_1_n, sumador_flags_1_v, sumador_flags_1_z;
  wire [3:0] and_1_out, inversor_4_1_s, or_1_out, sumador_flags_1_s;

  not not_1 (not_1_out, B[0]);
  not not_2 (not_2_out, B[1]);
  not not_3 (not_3_out, B[2]);
  and and_1 (and_1_out[0], A[0], B[0]);
  and and_2 (and_1_out[1], A[1], B[1]);
  and and_3 (and_1_out[2], A[2], B[2]);
  and and_4 (and_1_out[3], A[3], B[3]);
  or or_1 (or_1_out[0], A[0], B[0]);
  or or_2 (or_1_out[1], A[1], B[1]);
  or or_3 (or_1_out[2], A[2], B[2]);
  or or_4 (or_1_out[3], A[3], B[3]);
  and and_5 (and_5_out, not_1_out, not_2_out);
  and and_6 (and_6_out, not_3_out, B[3]);
  not not_4 (not_4_out, A[3]);
  and and_7 (and_7_out, and_5_out, and_6_out);
  and and_8 (and_8_out, OP[0], and_7_out);
  inversor_4 inversor_4_1 (.A(B), .INV(OP[0]), .S(inversor_4_1_s));
  and and_9 (and_9_out, and_8_out, not_4_out);
  and op11 (op11_out, OP[0], OP[1]);
  not not_5 (not_5_out, comparador_cero_1_z);
  comparador_cero comparador_cero_1 (.A(B), .Z(comparador_cero_1_z));
  Multiplexer multiplexer_1 (.in0(and_1_out[3]), .in1(or_1_out[3]), .out(multiplexer_1_out), .sel(op11_out));
  not not_6 (not_6_out, sumador_flags_1_c);
  sumador_flags sumador_flags_1 (
    .A(A), .B(inversor_4_1_s), .S(sumador_flags_1_s), .Z(sumador_flags_1_z), .V(sumador_flags_1_v),
    .N(sumador_flags_1_n), .C(sumador_flags_1_c));  // open: Cin
  and and_10 (and_10_out, OP[0], and_7_out);
  comparador_cero comparador_cero_2 (.A(S), .Z(comparador_cero_2_z));
  Multiplexer #(.select(2), .width(4)) multiplexer_2 (
    .in0(sumador_flags_1_s), .in1(sumador_flags_1_s), .in2(and_1_out), .in3(or_1_out), .out(S), .sel(OP));
  Multiplexer multiplexer_3 (.in0(sumador_flags_1_v), .in1(and_9_out), .out(multiplexer_3_out), .sel(and_10_out));
  and and_11 (and_11_out, not_6_out, not_5_out);
  Multiplexer multiplexer_4 (.in0(sumador_flags_1_z), .in1(comparador_cero_2_z), .out(Z), .sel(OP[1]));
  Multiplexer multiplexer_5 (.in0(multiplexer_3_out), .in1(1'b0), .out(multiplexer_5_out), .sel(OP[1]));
  Multiplexer multiplexer_6 (.in0(sumador_flags_1_n), .in1(multiplexer_1_out), .out(N), .sel(OP[1]));
  Multiplexer multiplexer_7 (.in0(sumador_flags_1_c), .in1(and_11_out), .out(multiplexer_7_out), .sel(OP[0]));
  Multiplexer multiplexer_8 (.in0(multiplexer_7_out), .in1(1'b0), .out(C), .sel(OP[1]));
  Multiplexer multiplexer_9 (.in0(multiplexer_5_out), .in1(multiplexer_7_out), .out(V), .sel(modo_sin_signo));

  // Notes on the sheet:
  //   a_es_negativo
  //   ALU  <3
  //   b_es_8
  //   op:and
  //   op:or
  //   es_resta
  //   detector_b_es_0_no_borrow
  //   0:and
  //   1:or
  //   ese_caso_de_la_resta
  //   00:suma
  //   01:resta
  //   10:and
  //   11:or
  //   0:suma_y_resta
  //   1:el_caso
  //   0:suma_y_resta
  //   1:and_y_or
  //   1:and_y_or
  //   0:suma_y_resta
  //   0:suma_y_resta
  //   1:and_y_or
  //   0:carry
  //   1:borrow
  //   0:suma_y_resta
  //   1:and_y_or
endmodule

module verificador (
  output [3:0] out_1,
  output [3:0] out_2,
  output [1:0] out_3,
  output halt,
  output N,
  output Z,
  output V,
  output C,
  output [3:0] res
);

  wire clock_1_out;

  Clock clock_1 (.out(clock_1_out));
  Counter #(.max('h3ff), .width(10)) counter_1 (
    .clk(clock_1_out), .carry(halt), .Q({out_3, out_2, out_1}));  // open: clr, load, up, count, D
  ALU alu_1 (.A(out_1), .B(out_2), .OP(out_3), .N(N), .Z(Z), .V(V), .C(C), .S(res));  // open: modo_sin_signo
endmodule
