// Logisim project TallerLogica_Combinatorios.circ as structural Verilog: 9 circuits, main circuit sumador_simple
module sumador_simple (
  input  A,
  input  B,
  output S,
  output Cout
);

  wire and_1_out, and_2_out, not_1_out, not_2_out;

  not not_1 (not_1_out, A);
  not not_2 (not_2_out, B);
  and and_1 (and_1_out, not_1_out, B);
  and and_2 (and_2_out, A, not_2_out);
  and and_3 (Cout, A, B);
  or or_1 (S, and_1_out, and_2_out);
endmodule

module sumador_completo (
  input  A,
  input  B,
  input  Cin,
  output S,
  output Cout
);

  wire sumador_simple_1_cout, sumador_simple_1_s, sumador_simple_2_cout;

  sumador_simple sumador_simple_1 (.A(A), .B(B), .S(sumador_simple_1_s), .Cout(sumador_simple_1_cout));
  sumador_simple sumador_simple_2 (.A(sumador_simple_1_s), .B(Cin), .S(S), .Cout(sumador_simple_2_cout));
  or or_1 (Cout, sumador_simple_2_cout, sumador_simple_1_cout);
endmodule

module sumador_4 (
  input  Cin,
  input  [3:0] A,
  input  [3:0] B,
  output [3:0] S,
  output Cout
);

  wire sumador_completo_1_cout, sumador_completo_2_cout, sumador_completo_3_cout;

  sumador_completo sumador_completo_1 (.A(A[0]), .B(B[0]), .Cin(Cin), .S(S[0]), .Cout(sumador_completo_1_cout));
  sumador_completo sumador_completo_2 (
    .A(A[1]), .B(B[1]), .Cin(sumador_completo_1_cout), .S(S[1]), .Cout(sumador_completo_2_cout));
  sumador_completo sumador_completo_3 (
    .A(A[2]), .B(B[2]), .Cin(sumador_completo_2_cout), .S(S[2]), .Cout(sumador_completo_3_cout));
  sumador_completo sumador_completo_4 (.A(A[3]), .B(B[3]), .Cin(sumador_completo_3_cout), .S(S[3]), .Cout(Cout));
  Hex_Digit_Display hex_digit_display_1 (.value(S));  // open: dp
endmodule

module comparador_cero (
  input  [3:0] A,
  output Z
);

  wire nor_1_out, nor_2_out;

  nor nor_1 (nor_1_out, A[0], A[1]);
  nor nor_2 (nor_2_out, A[2], A[3]);
  and and_1 (Z, nor_1_out, nor_2_out);
endmodule

module sumador_flags (
  input  Cin,
  input  [3:0] B,
  input  [3:0] A,
  output [3:0] S,
  output Z,
  output V,
  output N,
  output C
);

  sumador_4 sumador_4_1 (.Cin(Cin), .A(B), .B(A), .S({N, S[2:0]}), .Cout(C));
  xor xor_1 (V, N, C);
  comparador_cero comparador_cero_1 (.A({N, S[2:0]}), .Z(Z));
  Hex_Digit_Display hex_digit_display_1 (.value({N, S[2:0]}));  // open: dp

  assign S[3] = N;

  // Notes on the sheet:
  //   detector_negativo
  //   detector_overflow
endmodule

module incrementador_4 (
  input  [3:0] A,
  output [3:0] S
);

  sumador_4 sumador_4_1 (.Cin(1'b1), .A(A), .S(S));  // open: B, Cout
  Hex_Digit_Display hex_digit_display_1 (.value(S));  // open: dp
endmodule

module inversor_4 (
  input  [3:0] A,
  input  INV,
  output [3:0] S
);

  wire and_1_out, and_2_out, and_3_out, and_8_out, not_1_out, or_1_out, or_3_out, undriven;
  wire [3:0] incrementador_4_1_s;

  buf or_1 (or_1_out, and_1_out);  // OR_Gate
  buf and_1 (and_1_out, INV);  // AND_Gate
  incrementador_4 incrementador_4_1 (.A(A), .S(incrementador_4_1_s));
  // OR_Gate or_2 has open pins: in0=and_2_out, out=open
  buf and_2 (and_2_out, not_1_out);  // AND_Gate
  not not_1 (not_1_out, INV);
  or or_3 (or_3_out, and_3_out, undriven);
  or or_4 (or_3_out, and_3_out, undriven);
  buf and_3 (and_3_out, INV);  // AND_Gate
  buf and_4 (S[0], incrementador_4_1_s[0]);  // AND_Gate
  buf and_5 (S[3], incrementador_4_1_s[1]);  // AND_Gate
  buf and_6 (S[1], incrementador_4_1_s[2]);  // AND_Gate
  and and_7 (S[2], incrementador_4_1_s[3], or_1_out);
  // OR_Gate or_5 has open pins: in0=and_8_out, out=open
  and and_8 (and_8_out, S[2], INV);
  Hex_Digit_Display hex_digit_display_1 (.value(S));  // open: dp
endmodule

module ALU (
  input  [3:0] A,
  input  [3:0] B,
  input  [1:0] OP,
  output N,
  output Z,
  output V,
  output C,
  output [3:0] S
);

  Hex_Digit_Display hex_digit_display_1 (.value(S));  // open: dp
endmodule

module verificador (
  output [3:0] out_1,
  output [3:0] out_2,
  output [1:0] out_3,
  output halt,
  output N,
  output Z,
  output V,
  output C,
  output [3:0] res
);

  wire clock_1_out;

  Clock clock_1 (.out(clock_1_out));
  Counter #(.max('h3ff), .width(10)) counter_1 (
    .clk(clock_1_out), .carry(halt), .Q({out_3, out_2, out_1}));  // open: clr, load, up, count, D
  ALU alu_1 (.A(out_1), .B(out_2), .OP(out_3), .N(N), .Z(Z), .V(V), .C(C), .S(res));
endmodule
